# Fritzing sketch hc05-configuration (saved by Fritzing 0.9.3b)
breadboards: 1

parts:
  Arduino_Uno = Arduino Uno (Rev3) - ICSP
  HC-05 = Bluetooth HC-05 Macho
  Resistor_1 = Resistor [tolerance=±5% resistance=1k package="2010 [SMD]"]
  Resistor_2 = Resistor [tolerance=±5% resistance=1k package="2512 [SMD]"]
  Resistor_3 = Resistor [tolerance=±5% resistance=1k package="2512 [SMD]"]

nets:
  N1: Arduino_Uno.D2, HC-05.TXD
  N2: Arduino_Uno.D3_PWM, Resistor_1.Pin_0
  5V: Arduino_Uno.5V, HC-05.VCC
  GND: Arduino_Uno.GND, HC-05.GND, Resistor_3.Pin_1
  N3: HC-05.RXD, Resistor_1.Pin_1, Resistor_2.Pin_0
  N4: Resistor_2.Pin_1, Resistor_3.Pin_0
